// Logisim project Memory-Project.circ as structural Verilog: 7 circuits, main circuit main
module main (
  input  in_1
);

  wire clock_1_out;

  Clock clock_1 (.out(clock_1_out));
  // D_Flip_Flop #(.trigger("falling")) d_ff_1: pin names not known; wires that end beside it: clock_1_out, in_1
  D_Flip_Flop #(.trigger("falling")) d_ff_2 ();  // open: clk, D, Q, Qn, preset, en, reset
  D_Flip_Flop #(.trigger("falling")) d_ff_3 ();  // open: clk, D, Q, Qn, preset, en, reset
  D_Flip_Flop #(.trigger("falling")) d_ff_4 ();  // open: clk, D, Q, Qn, preset, en, reset
  D_Flip_Flop #(.trigger("falling")) d_ff_5 ();  // open: clk, D, Q, Qn, preset, en, reset
  D_Flip_Flop #(.trigger("falling")) d_ff_6 ();  // open: clk, D, Q, Qn, preset, en, reset
  D_Flip_Flop #(.trigger("falling")) d_ff_7 ();  // open: clk, D, Q, Qn, preset, en, reset
  D_Flip_Flop #(.trigger("falling")) d_ff_8 ();  // open: clk, D, Q, Qn, preset, en, reset
  D_Flip_Flop #(.trigger("falling")) d_ff_9 ();  // open: clk, D, Q, Qn, preset, en, reset
  D_Flip_Flop #(.trigger("falling")) d_ff_10 ();  // open: clk, D, Q, Qn, preset, en, reset
  D_Flip_Flop #(.trigger("falling")) d_ff_11 ();  // open: clk, D, Q, Qn, preset, en, reset
endmodule

module counter (
  input  [11:0] D_input,
  output [11:0] \output 
);

  wire clock_out, comparator_1_gt, or_1_out;
  wire [11:0] complementary_2_12_bit_lookahead_adder_1_p4;

  Comparator #(.width(12)) comparator_1 (.a(\output ), .b(D_input), .gt(comparator_1_gt));  // open: eq, lt
  Clock clock (.out(clock_out));
  // complementary_2_12_bit_lookahead_adder complementary_2_12_bit_lookahead_adder_1: pin names not known; wires that end beside it: \output , {12{1'b0}}, 1'b1, complementary_2_12_bit_lookahead_adder_1_p4
  or or_1 (or_1_out, \output [11], comparator_1_gt);
  _12_bit_Register u_12_bit_register_1 (
    .D(complementary_2_12_bit_lookahead_adder_1_p4), .Reset(or_1_out), .Write(1'b1), .C(clock_out),
    .Q(\output ));
endmodule

module _12_bit_Register (
  input  [11:0] D,
  input  Reset,
  input  Write,
  input  C,
  output [11:0] Q
);

  wire d_ff_2_qn, d_ff_7_qn, d_ff_10_qn, d_ff_13_qn, undriven, undriven_2, undriven_3, undriven_4, undriven_5;

  D_Flip_Flop #(.trigger("falling")) d_ff_1 (
    .clk(C), .D(D[0]), .Q(Q[0]), .en(undriven_5), .reset(Reset));  // open: Qn, preset
  D_Flip_Flop #(.trigger("falling")) d_ff_2 (
    .clk(C), .D(D[1]), .Q(Q[1]), .Qn(d_ff_2_qn), .preset(undriven), .en(undriven_5), .reset(Reset));
  D_Flip_Flop #(.trigger("falling")) d_ff_3 (
    .clk(C), .D(D[1]), .Q(Q[1]), .Qn(d_ff_2_qn), .preset(undriven), .en(undriven_5), .reset(Reset));
  D_Flip_Flop #(.trigger("falling")) d_ff_4 (
    .clk(C), .D(D[3]), .Q(Q[3]), .en(undriven_5), .reset(Reset));  // open: Qn, preset
  D_Flip_Flop #(.trigger("falling")) d_ff_5 (
    .clk(C), .D(D[4]), .Q(Q[4]), .en(undriven_5), .reset(Reset));  // open: Qn, preset
  D_Flip_Flop #(.trigger("falling")) d_ff_6 (
    .clk(C), .D(D[5]), .Q(Q[5]), .en(undriven_5), .reset(Reset));  // open: Qn, preset
  D_Flip_Flop #(.trigger("falling")) d_ff_7 (
    .clk(C), .D(D[6]), .Q(Q[6]), .Qn(d_ff_7_qn), .preset(undriven_2), .en(undriven_5), .reset(Reset));
  D_Flip_Flop #(.trigger("falling")) d_ff_8 (
    .clk(C), .D(D[6]), .Q(Q[6]), .Qn(d_ff_7_qn), .preset(undriven_2), .en(undriven_5), .reset(Reset));
  D_Flip_Flop #(.trigger("falling")) d_ff_9 (
    .clk(C), .D(D[7]), .Q(Q[7]), .en(undriven_5), .reset(Reset));  // open: Qn, preset
  D_Flip_Flop #(.trigger("falling")) d_ff_10 (
    .clk(C), .D(D[8]), .Q(Q[8]), .Qn(d_ff_10_qn), .preset(undriven_3), .en(undriven_5), .reset(Reset));
  D_Flip_Flop #(.trigger("falling")) d_ff_11 (
    .clk(C), .D(D[8]), .Q(Q[8]), .Qn(d_ff_10_qn), .preset(undriven_3), .en(undriven_5), .reset(Reset));
  D_Flip_Flop #(.trigger("falling")) d_ff_12 (
    .clk(C), .D(D[9]), .Q(Q[9]), .en(undriven_5), .reset(Reset));  // open: Qn, preset
  D_Flip_Flop #(.trigger("falling")) d_ff_13 (
    .clk(C), .D(D[10]), .Q(Q[10]), .Qn(d_ff_13_qn), .preset(undriven_4), .en(undriven_5), .reset(Reset));
  D_Flip_Flop #(.trigger("falling")) d_ff_14 (
    .clk(C), .D(D[10]), .Q(Q[10]), .Qn(d_ff_13_qn), .preset(undriven_4), .en(undriven_5), .reset(Reset));
  D_Flip_Flop #(.trigger("falling")) d_ff_15 (
    .clk(C), .D(D[11]), .Q(Q[11]), .en(undriven_5), .reset(Reset));  // open: Qn, preset
endmodule

module Register_File (
  input  in_1,
  input  [11:0] in_2,
  input  in_3,
  input  [7:0] in_4,
  output out_5,
  output [11:0] out_6
);

  wire n4_bit_lookahead_adder_1_p1, n4_bit_lookahead_adder_1_p2, n4_bit_lookahead_adder_1_p14,
       n4_bit_lookahead_adder_1_p17, n4_bit_lookahead_adder_1_p18, n4_bit_lookahead_adder_1_p19,
       n4_bit_lookahead_adder_1_p20, n4_bit_lookahead_adder_1_p21, n4_bit_lookahead_adder_1_p30,
       n4_bit_lookahead_adder_1_p31, n4_bit_lookahead_adder_1_p48, n4_bit_lookahead_adder_1_p49,
       n4_bit_lookahead_adder_1_p50, n4_bit_lookahead_adder_1_p51, n4_bit_lookahead_adder_1_p53;
  wire [11:0] n4_bit_lookahead_adder_1_p3, r2_q;

  // AND_Gate g0 has open pins: in1=n4_bit_lookahead_adder_1_p1, out=open
  _12_bit_Register r2 (
    .D(n4_bit_lookahead_adder_1_p3), .Reset(n4_bit_lookahead_adder_1_p1),
    .Write(n4_bit_lookahead_adder_1_p14), .C(n4_bit_lookahead_adder_1_p2), .Q(r2_q));
  // AND_Gate and_1 is placed but not wired
  // _4_bit_lookahead_adder 4_bit_lookahead_adder_1: pin names not known; wires that end beside it: n4_bit_lookahead_adder_1_p1, n4_bit_lookahead_adder_1_p2, n4_bit_lookahead_adder_1_p3, n4_bit_lookahead_adder_1_p2, n4_bit_lookahead_adder_1_p3, n4_bit_lookahead_adder_1_p1, n4_bit_lookahead_adder_1_p2, n4_bit_lookahead_adder_1_p3, n4_bit_lookahead_adder_1_p1, n4_bit_lookahead_adder_1_p2, n4_bit_lookahead_adder_1_p3, n4_bit_lookahead_adder_1_p1, n4_bit_lookahead_adder_1_p2, n4_bit_lookahead_adder_1_p14, n4_bit_lookahead_adder_1_p14, n4_bit_lookahead_adder_1_p14, n4_bit_lookahead_adder_1_p17, n4_bit_lookahead_adder_1_p18, n4_bit_lookahead_adder_1_p19, n4_bit_lookahead_adder_1_p20, n4_bit_lookahead_adder_1_p21, in_3, out_5, n4_bit_lookahead_adder_1_p17, n4_bit_lookahead_adder_1_p18, r2_q, n4_bit_lookahead_adder_1_p19, n4_bit_lookahead_adder_1_p20, n4_bit_lookahead_adder_1_p21, n4_bit_lookahead_adder_1_p30, n4_bit_lookahead_adder_1_p31, n4_bit_lookahead_adder_1_p17, n4_bit_lookahead_adder_1_p18, r2_q, n4_bit_lookahead_adder_1_p19, n4_bit_lookahead_adder_1_p20, n4_bit_lookahead_adder_1_p21, n4_bit_lookahead_adder_1_p30, n4_bit_lookahead_adder_1_p31, n4_bit_lookahead_adder_1_p17, n4_bit_lookahead_adder_1_p18, r2_q, n4_bit_lookahead_adder_1_p19, n4_bit_lookahead_adder_1_p20, n4_bit_lookahead_adder_1_p21, n4_bit_lookahead_adder_1_p30, n4_bit_lookahead_adder_1_p31, n4_bit_lookahead_adder_1_p48, n4_bit_lookahead_adder_1_p49, n4_bit_lookahead_adder_1_p50, n4_bit_lookahead_adder_1_p51, out_6, n4_bit_lookahead_adder_1_p53
  // OR_Gate or_1: pin names not known
endmodule

module C2 (
  input  in_1,
  input  [7:0] in_2,
  output out_3
);

  wire and_1_out, and_2_out, g0_out, g1_out, p0_out, p1_out;

  or p0 (p0_out, in_2[0], in_2[1]);
  and g0 (g0_out, in_2[0], in_2[1]);
  or p1 (p1_out, in_2[2], in_2[3]);
  and g1 (g1_out, in_2[3], in_2[2]);
  and and_1 (and_1_out, in_1, p0_out, p1_out);
  and and_2 (and_2_out, g0_out, p1_out);
  or or_1 (out_3, and_1_out, and_2_out, g1_out);
endmodule

module C3 (
  input  in_1,
  input  [7:0] in_2,
  output out_3
);

  wire and_1_out, and_2_out, and_3_out, g0_out, g1_out, g2_out, p0_out, p1_out, p2_out;

  or p0 (p0_out, in_2[1], in_2[0]);
  and g0 (g0_out, in_2[1], in_2[0]);
  or p1 (p1_out, in_2[3], in_2[2]);
  and g1 (g1_out, in_2[3], in_2[2]);
  or p2 (p2_out, in_2[5], in_2[4]);
  and g2 (g2_out, in_2[5], in_2[4]);
  and and_1 (and_1_out, in_1, p0_out, p1_out, p2_out);
  and and_2 (and_2_out, g0_out, p1_out, p2_out);
  and and_3 (and_3_out, g1_out, p2_out);
  or or_1 (out_3, and_1_out, and_2_out, and_3_out, g2_out);
endmodule

module C4 (
  input  C0,
  input  CARRY_IN,
  input  A,
  input  B,
  input  [7:0] in_5,
  output SUM,
  output [11:0] out_7,
  output out_8
);

  wire and_1_out, and_2_out, and_3_out, g0_out, g1_out, g2_out, g3_out, p0_out, p1_out, p3_out, undriven,
       xor_1_p1;

  or p0 (p0_out, in_5[0], in_5[1]);
  and g0 (g0_out, in_5[0], in_5[1]);
  or p1 (p1_out, in_5[2], in_5[3]);
  and g1 (g1_out, in_5[2], in_5[3]);
  and g2 (g2_out, in_5[4], in_5[5]);
  or p3 (p3_out, in_5[6], in_5[7]);
  and g3 (g3_out, in_5[7], in_5[6]);
  and and_1 (and_1_out, C0, p0_out, p1_out, undriven, p3_out);
  and and_2 (and_2_out, g1_out, undriven, p3_out);
  and and_3 (and_3_out, g2_out, p3_out);
  // XOR_Gate #(.\xor ("odd")) xor_1: pin names not known; wires that end beside it: xor_1_p1
  // AND_Gate and_4: pin names not known
  // AND_Gate and_5: pin names not known; wires that end beside it: and_2_out, and_2_out
  Multiplexer #(.select(3), .width(12), .enable("false")) multiplexer_1 ();  // open: in0, in1, in2, in3, in4, in5, in6, in7, out, sel
  or or_1 (out_7[0], and_1_out, xor_1_p1, and_2_out, and_3_out, g3_out);
  // OR_Gate or_2 is placed but not wired
  // Pins of 1 and 12 bits meet at out_7

  // Notes on the sheet:
  //   CARRY OUT
endmodule
